# Fritzing sketch DHT22Sketch (saved by Fritzing 0.9.2b)
breadboards: 1

parts:
  Raspberry_Pi1 = Raspberry Pi 2
  RHT1 = Humidity and Temperature Sensor RHT03

nets:
  3V3: Raspberry_Pi1.3v3, RHT1.Vcc
  N1: Raspberry_Pi1.GPIO4, RHT1.Data-signal
  N2: Raspberry_Pi1.GND, RHT1.GND_2
